// Digital circuit signal generator and character indexer.dig as structural Verilog
module signal_generator_and_character_indexer (
  input  pxl
);

  wire _7404_1_pin3, _7404_1_pin4, _7404_1_pin5, _7404_1_pin6, _7404_2_pin2, _7404_2_pin4, _7404_2_pin6,
       _7404_2_pin8, _7404_2_pin10, _7404_2_pin12, _7404_3_pin8, _7404_3_pin10, _7404_3_pin12, _7421_1_pin4,
       _7421_1_pin5, _7421_1_pin9, _7421_1_pin10, _7421_1_pin12, _7421_1_pin13, _7458_1_pin6, _7458_1_pin8,
       _7458_2_pin6, _7458_2_pin8, _74161_1_pin1, _74161_1_pin11, _74161_1_pin12, _74161_1_pin13,
       _74161_1_pin14, _74161_2_pin11, _74161_2_pin12, _74161_2_pin13, _74161_2_pin14, _74161_2_pin15,
       _74161_3_pin11, _74161_3_pin14, _74161_4_pin13, _74161_4_pin15, _74161_5_pin11, _74161_5_pin12,
       _74161_5_pin13, _74161_5_pin14, _74161_5_pin15, _74161_6_pin14, _744075_1_pin3, _744075_1_pin4,
       _744075_1_pin6, _744075_1_pin8, _744075_1_pin9, _744075_1_pin10, _744075_1_pin13, _744075_2_pin9,
       _744075_2_pin10, not_1_out;

  _74161 _74161_1 (
    .pin1(_74161_1_pin1), .pin2(pxl), .pin3(1'b0), .pin4(1'b0), .pin5(1'b0), .pin6(1'b0), .pin7(1'b1),
    .pin8(1'b0), .pin9(1'b1), .pin10(1'b1), .pin11(_74161_1_pin11), .pin12(_74161_1_pin12),
    .pin13(_74161_1_pin13), .pin14(_74161_1_pin14), .pin16(1'b1));  // open: pin15
  _7404 _7404_1 (
    .pin1(_74161_1_pin11), .pin2(_74161_1_pin1), .pin3(_7404_1_pin3), .pin4(_7404_1_pin4),
    .pin5(_7404_1_pin5), .pin6(_7404_1_pin6), .pin7(1'b0), .pin9(1'b0), .pin11(1'b0), .pin13(1'b0),
    .pin14(1'b1));  // open: pin8, pin10, pin12
  _74161 _74161_2 (
    .pin1(_7404_1_pin6), .pin2(_74161_1_pin11), .pin3(1'b0), .pin4(1'b0), .pin5(1'b0), .pin6(1'b0),
    .pin7(1'b1), .pin8(1'b0), .pin9(1'b1), .pin10(1'b1), .pin11(_74161_2_pin11), .pin12(_74161_2_pin12),
    .pin13(_74161_2_pin13), .pin14(_74161_2_pin14), .pin15(_74161_2_pin15), .pin16(1'b1));
  _7421 _7421_1 (
    .pin1(_74161_2_pin12), .pin2(1'b1), .pin4(_7421_1_pin4), .pin5(_7421_1_pin5), .pin6(_7404_1_pin5),
    .pin7(1'b0), .pin8(_7404_1_pin3), .pin9(_7421_1_pin9), .pin10(_7421_1_pin10), .pin12(_7421_1_pin12),
    .pin13(_7421_1_pin13), .pin14(1'b1));  // open: pin3, pin11
  _74161 _74161_3 (
    .pin1(_7404_1_pin6), .pin2(_74161_1_pin11), .pin3(1'b0), .pin4(1'b0), .pin5(1'b0), .pin6(1'b0),
    .pin7(1'b1), .pin8(1'b0), .pin9(1'b1), .pin10(_74161_2_pin15), .pin11(_74161_3_pin11),
    .pin12(_7421_1_pin4), .pin13(_7421_1_pin5), .pin14(_74161_3_pin14), .pin16(1'b1));  // open: pin15
  _74161 _74161_4 (
    .pin1(_7404_1_pin4), .pin2(_7404_1_pin6), .pin3(1'b0), .pin4(1'b0), .pin5(1'b0), .pin6(1'b0),
    .pin7(1'b1), .pin8(1'b0), .pin9(1'b1), .pin10(1'b1), .pin11(_7421_1_pin12), .pin12(_7421_1_pin10),
    .pin13(_74161_4_pin13), .pin14(_7421_1_pin9), .pin15(_74161_4_pin15), .pin16(1'b1));
  _74161 _74161_5 (
    .pin1(_7404_1_pin4), .pin2(_7404_1_pin6), .pin3(1'b0), .pin4(1'b0), .pin5(1'b0), .pin6(1'b0),
    .pin7(1'b1), .pin8(1'b0), .pin9(1'b1), .pin10(_74161_4_pin15), .pin11(_74161_5_pin11),
    .pin12(_74161_5_pin12), .pin13(_74161_5_pin13), .pin14(_74161_5_pin14), .pin15(_74161_5_pin15),
    .pin16(1'b1));
  _74161 _74161_6 (
    .pin1(_7404_1_pin4), .pin2(_7404_1_pin6), .pin3(1'b0), .pin4(1'b0), .pin5(1'b0), .pin6(1'b0),
    .pin7(1'b1), .pin8(1'b0), .pin9(1'b1), .pin10(_74161_5_pin15), .pin13(_7421_1_pin13),
    .pin14(_74161_6_pin14), .pin16(1'b1));  // open: pin11, pin12, pin15
  not not_1 (not_1_out, _7421_1_pin13);
  _7404 _7404_2 (
    .pin1(_74161_2_pin13), .pin2(_7404_2_pin2), .pin3(_74161_2_pin12), .pin4(_7404_2_pin4),
    .pin5(_74161_2_pin11), .pin6(_7404_2_pin6), .pin7(1'b0), .pin8(_7404_2_pin8), .pin9(_74161_3_pin14),
    .pin10(_7404_2_pin10), .pin11(_7421_1_pin5), .pin12(_7404_2_pin12), .pin13(_7421_1_pin4), .pin14(1'b1));
  _744075 _744075_1 (
    .pin1(_7421_1_pin10), .pin2(_74161_5_pin14), .pin3(_744075_1_pin3), .pin4(_744075_1_pin4), .pin5(1'b0),
    .pin6(_744075_1_pin6), .pin7(1'b0), .pin8(_744075_1_pin8), .pin9(_744075_1_pin9),
    .pin10(_744075_1_pin10), .pin11(_744075_1_pin9), .pin12(_744075_1_pin6), .pin13(_744075_1_pin13),
    .pin14(1'b1));
  _7404 _7404_3 (
    .pin1(_74161_4_pin13), .pin2(_744075_1_pin8), .pin3(_7421_1_pin12), .pin4(_744075_1_pin4),
    .pin5(_74161_5_pin13), .pin6(_744075_1_pin3), .pin7(1'b0), .pin8(_7404_3_pin8), .pin9(_74161_5_pin12),
    .pin10(_7404_3_pin10), .pin11(_74161_5_pin11), .pin12(_7404_3_pin12), .pin13(_74161_6_pin14), .pin14(1'b1));
  _7458 _7458_1 (
    .pin1(not_1_out), .pin2(not_1_out), .pin3(_744075_1_pin3), .pin4(not_1_out), .pin5(_7404_3_pin8),
    .pin6(_7458_1_pin6), .pin7(1'b0), .pin8(_7458_1_pin8), .pin9(1'b1), .pin10(_7404_3_pin12),
    .pin11(not_1_out), .pin12(1'b1), .pin13(_7404_3_pin10), .pin14(1'b1));
  _7458 _7458_2 (
    .pin1(_7404_2_pin2), .pin2(_7404_2_pin12), .pin3(1'b1), .pin4(_7404_2_pin10), .pin5(_7404_2_pin8),
    .pin6(_7458_2_pin6), .pin7(1'b0), .pin8(_7458_2_pin8), .pin9(_74161_2_pin11), .pin10(_74161_2_pin12),
    .pin11(_74161_2_pin13), .pin12(_7404_2_pin6), .pin13(_7404_2_pin4), .pin14(1'b1));
  _744075 _744075_2 (
    .pin1(_7404_2_pin12), .pin2(_7404_2_pin8), .pin3(_7404_3_pin8), .pin4(_7404_3_pin10),
    .pin5(_7404_3_pin12), .pin6(_744075_1_pin13), .pin7(1'b0), .pin8(_7458_2_pin8), .pin9(_744075_2_pin9),
    .pin10(_744075_2_pin10), .pin11(1'b0), .pin12(_7458_1_pin8), .pin13(_7458_1_pin6), .pin14(1'b1));
  VGA vga_1 (.R(1'b0), .G(1'b0), .B(1'b1), .H(_744075_2_pin9), .V(_744075_1_pin10), .C(pxl));

  // Notes on the sheet:
  //   pxl: Hz: 2147483647
  //   Frame completion pulse
  //   Horizontal character counter
  //   Pixel clock divider
  //   Line completion pulse
  //   Line counter
  //   Character pixel horizontal (0-7)
  //   Character index horizontal (0-99)
  //   3 lines below are also character
  //   pixel vertical
  //   Current line vertical (0-524)
  //   Shifting current line bus left 3 bits
  //   should also give current vertical
  //   character
  //   !C
  //   !G
  //   !D
  //   !E
  //   !F
  //   High during hvis
  //   Low during hsync
  //   High during vvis
  //   Low during vsync
  //   Can the pulsegen be made smaller?
  //   Probably. Front/back porch do
  //   not need to be pulsed.
  //   All we want is:
  //   - hsync line that goes low during hsync, stays high else
  //   - vis line that goes low during blanking, stays high else
endmodule
